# Fritzing sketch line-follower (saved by Fritzing 0.9.3b)

parts:
  M3 = DC Motor  # not connected
  M4 = DC Motor  # not connected
  M5 = fc-51 [package=THT]
  M7 = fc-51 [package=THT]
  VCC1 = 4 x AAA Battery Mount
  U2 = SWITCH_SPDT [package=kps-1290]
  Mod1 = Raspberry Pi 4 B+
  M8 = fc-51 [package=THT]
  M9 = fc-51 [package=THT]
  M10 = fc-51 [package=THT]
  L298N2 = L298N DC motor driver

nets:
  N1: M5.pin1, Mod1.GPIO26
  N2: M7.pin1, Mod1.GPIO17
  N3: VCC1.-, L298N2.GND
  N4: VCC1.+, U2.S
  N5: U2.O, L298N2.12V
  5V: Mod1.5V, L298N2.5V
  N6: Mod1.GPIO4, M9.pin1
  N7: Mod1.GPIO27, M10.pin1
  N8: Mod1.GPIO22, M8.pin1
  N9: Mod1.GPIO23, L298N2.IN1
  N10: Mod1.GPIO24, L298N2.IN2
  N11: Mod1.GPIO12, L298N2.ENB
  N12: Mod1.GPIO13, L298N2.ENA
  N13: Mod1.GPIO20, L298N2.IN3
  N14: Mod1.GPIO21, L298N2.IN4

notes:
  Left Motor
  Right Motor

custom parts:
  Raspberry Pi 4 B+: The RPi4B, a faster version of the awesome Raspberry Pi 3 ARM Board with 40 pin gpio. Ready for special Raspberry Pi B+ and RPi2 Hat (Hardware attached (on) top) new features: The most surprising change for the Pi 4B is that it is available with three different amounts of fast DDR4 SDRAM memory; 1GB, 2GB, or 4GB. Combined with a newer 1.5GHz quad-core processor, the Pi 4B can run larger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
  L298N DC motor driver: 2x DC motor driver with 78M05 positive voltage regulator (7..35 V) L298N: max 46 V, 2 A Set 5 V Enable jumper to enable 5 V regultor (needed for the L298N) and +5 V output at screw terminal or supply external +5 V at screw terminal Set ENA and/or ENB to +5 V to enable motor permanently or supply ENA and/or ENB with PWM signal IN1 and IN2 set rotation directory for motor A (OUT1/OUT2) IN2 and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
