# Fritzing sketch line-follower0 (saved by Fritzing 0.9.3b)

parts:
  L298N2 = L298N DC motor driver
  M3 = DC Motor  # not connected
  M4 = DC Motor  # not connected
  M5 = fc-51 [package=THT]
  M7 = fc-51 [package=THT]
  VCC1 = 4 x AAA Battery Mount
  U2 = SWITCH_SPDT [package=kps-1290]
  Mod1 = Raspberry Pi 4 B+
  M8 = fc-51 [package=THT]
  L298N3 = L298N DC motor driver  # not connected

nets:
  N1: L298N2.12V, U2.O
  N2: L298N2.GND, VCC1.-
  N3: L298N2.5V#7, Mod1.5V
  N4: L298N2.5V#9, L298N2.ENA
  N5: L298N2.5V#10, L298N2.ENB
  N6: L298N2.IN1, Mod1.GPIO23
  N7: L298N2.IN2, Mod1.GPIO24
  N8: L298N2.IN3, Mod1.GPIO20
  N9: L298N2.IN4, Mod1.GPIO21
  N10: M5.pin1, Mod1.GPIO26
  N11: M7.pin1, Mod1.GPIO17
  N12: VCC1.+, U2.S
  N13: Mod1.GPIO22, M8.pin1

notes:
  Left Motor
  Right Motor

custom parts:
  L298N DC motor driver: 2x DC motor driver with 78M05 positive voltage regulator (7..35 V) L298N: max 46 V, 2 A Set 5 V Enable jumper to enable 5 V regultor (needed for the L298N) and +5 V output at screw terminal or supply external +5 V at screw terminal Set ENA and/or ENB to +5 V to enable motor permanently or supply ENA and/or ENB with PWM signal IN1 and IN2 set rotation directory for motor A (OUT1/OUT2) IN2 and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
  Raspberry Pi 4 B+: The RPi4B, a faster version of the awesome Raspberry Pi 3 ARM Board with 40 pin gpio. Ready for special Raspberry Pi B+ and RPi2 Hat (Hardware attached (on) top) new features: The most surprising change for the Pi 4B is that it is available with three different amounts of fast DDR4 SDRAM memory; 1GB, 2GB, or 4GB. Combined with a newer 1.5GHz quad-core processor, the Pi 4B can run larger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
