# Fritzing sketch Connection_Raspberry_HC-SR04 (saved by Fritzing 0.9.3b)

parts:
  HC-SR04_Sensor_1 = HC-SR04 Ultrasonic Distance Sensor
  Mod1 = Raspberry Pi 4 B+

nets:
  VCC: HC-SR04_Sensor_1.VCC, Mod1.5V
  N1: HC-SR04_Sensor_1.TRIG, Mod1.GPIO4
  N2: HC-SR04_Sensor_1.ECHO, Mod1.GPIO27
  GND: HC-SR04_Sensor_1.GND, Mod1.GND

custom parts:
  Raspberry Pi 4 B+: The RPi4B, a faster version of the awesome Raspberry Pi 3 ARM Board with 40 pin gpio. Ready for special Raspberry Pi B+ and RPi2 Hat (Hardware attached (on) top) new features: The most surprising change for the Pi 4B is that it is available with three different amounts of fast DDR4 SDRAM memory; 1GB, 2GB, or 4GB. Combined with a newer 1.5GHz quad-core processor, the Pi 4B can run larger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
