# Fritzing sketch IR-Proximity_RaspberryPi3 (saved by Fritzing 0.9.3b)

parts:
  M1 = fc-51 [package=THT]
  Mod1 = Raspberry Pi 4 B+
  M2 = fc-51 [package=THT]
  M3 = fc-51 [package=THT]

nets:
  N1: M1.pin1, Mod1.GPIO17
  N2: M1.pin2, Mod1.GND
  N3: M1.pin3, Mod1.3V3
  N4: Mod1.GPIO22, M2.pin1
  N5: Mod1.GPIO26, M3.pin1

custom parts:
  fc-51: Fc-51 Infrared Obstacle Avoidance Proximity Sensor module. IR transmitter led, receiver LED, lm393 compaitor and a pot. 3.3 V to 5V power.
  Raspberry Pi 4 B+: The RPi4B, a faster version of the awesome Raspberry Pi 3 ARM Board with 40 pin gpio. Ready for special Raspberry Pi B+ and RPi2 Hat (Hardware attached (on) top) new features: The most surprising change for the Pi 4B is that it is available with three different amounts of fast DDR4 SDRAM memory; 1GB, 2GB, or 4GB. Combined with a newer 1.5GHz quad-core processor, the Pi 4B can run larger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
