# Fritzing sketch L298N-Module_RaspberryPi (saved by Fritzing 0.9.3b)

parts:
  L298N1 = L298N DC motor driver
  M1 = DC Motor
  M2 = DC Motor
  Mod1 = Raspberry Pi 4 B+
  VCC2 = 4 x AAA Battery Mount
  U3 = SWITCH_SPDT [package=kps-1290]

nets:
  N1: L298N1.OUT1, M2.pin_2
  N2: L298N1.OUT2, M2.pin_1
  N3: L298N1.OUT3, M1.pin_2
  N4: L298N1.OUT4, M1.pin_1
  N5: L298N1.12V, U3.S
  N6: L298N1.GND, VCC2.-
  5V: L298N1.5V, Mod1.5V
  N7: L298N1.ENA, Mod1.GPIO12
  N8: L298N1.ENB, Mod1.GPIO13
  N9: L298N1.IN1, Mod1.GPIO23
  N10: L298N1.IN2, Mod1.GPIO24
  N11: L298N1.IN3, Mod1.GPIO20
  N12: L298N1.IN4, Mod1.GPIO21
  N13: VCC2.+, U3.O

notes:
  Left Motor
  Right Motor
  L298N Motor Driver Board

custom parts:
  L298N DC motor driver: 2x DC motor driver with 78M05 positive voltage regulator (7..35 V) L298N: max 46 V, 2 A Set 5 V Enable jumper to enable 5 V regultor (needed for the L298N) and +5 V output at screw terminal or supply external +5 V at screw terminal Set ENA and/or ENB to +5 V to enable motor permanently or supply ENA and/or ENB with PWM signal IN1 and IN2 set rotation directory for motor A (OUT1/OUT2) IN2 and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
  Raspberry Pi 4 B+: The RPi4B, a faster version of the awesome Raspberry Pi 3 ARM Board with 40 pin gpio. Ready for special Raspberry Pi B+ and RPi2 Hat (Hardware attached (on) top) new features: The most surprising change for the Pi 4B is that it is available with three different amounts of fast DDR4 SDRAM memory; 1GB, 2GB, or 4GB. Combined with a newer 1.5GHz quad-core processor, the Pi 4B can run larger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
